// Logisim project cr8.circ as structural Verilog: 9 circuits, main circuit dflop
module main (
);

  wire CLK;
  wire [7:0] A_q, ACC_q, alu_1_q, alu_1_zf, B_q, C_q, controlled_buffer_1_out, controlled_buffer_13_out,
       controlled_buffer_15_out, controlled_buffer_17_out, D_q, F_q, H_q, K_q, L_q, mem_1_d_out, PCH_q,
       PCL_q, Z_q;

  Clock clock_1 (.out(CLK));
  assign controlled_buffer_1_out = 1'b0 ? 8'hf4 : 8'bz;  // Controlled_Buffer controlled_buffer_1
  Register B (.D(controlled_buffer_1_out), .en(1'b0), .clk(CLK), .Q(B_q));  // open: clr
  Register A (.D(controlled_buffer_1_out), .en(1'b0), .clk(CLK), .Q(A_q));  // open: clr
  assign controlled_buffer_1_out = 1'b0 ? B_q : 8'bz;  // Controlled_Buffer controlled_buffer_2
  assign controlled_buffer_1_out = 1'b0 ? A_q : 8'bz;  // Controlled_Buffer controlled_buffer_3
  Register D (.D(controlled_buffer_1_out), .en(1'b0), .clk(CLK), .Q(D_q));  // open: clr
  Register C (.D(controlled_buffer_1_out), .en(1'b0), .clk(CLK), .Q(C_q));  // open: clr
  assign controlled_buffer_1_out = 1'b0 ? D_q : 8'bz;  // Controlled_Buffer controlled_buffer_4
  assign controlled_buffer_1_out = 1'b0 ? C_q : 8'bz;  // Controlled_Buffer controlled_buffer_5
  Register ACC (.D(controlled_buffer_1_out), .en(1'b0), .clk(CLK), .Q(ACC_q));  // open: clr
  Register F (.D(controlled_buffer_1_out), .en(1'b0), .clk(CLK), .Q(F_q));  // open: clr
  Register Z (.D(controlled_buffer_1_out), .en(1'b0), .clk(CLK), .Q(Z_q));  // open: clr
  assign controlled_buffer_1_out = 1'b0 ? F_q : 8'bz;  // Controlled_Buffer controlled_buffer_6
  assign controlled_buffer_1_out = 1'b0 ? Z_q : 8'bz;  // Controlled_Buffer controlled_buffer_7
  Register K (.D(controlled_buffer_1_out), .en(1'b0), .clk(CLK), .Q(K_q));  // open: clr
  assign controlled_buffer_1_out = 1'b0 ? K_q : 8'bz;  // Controlled_Buffer controlled_buffer_8
  alu alu_1 (
    .CLK(CLK), .CS(1'b0), .SUB(1'b0), .CF_in(F_q[2]), .BF_in(F_q[3]), .A(ACC_q), .B(controlled_buffer_1_out),
    .CF(alu_1_zf[2]), .BF(alu_1_zf[3]), .ZF(alu_1_zf[0]), .Q(alu_1_q));
  assign controlled_buffer_1_out = 1'b0 ? alu_1_q : 8'bz;  // Controlled_Buffer controlled_buffer_9
  assign controlled_buffer_1_out = 1'b0 ? alu_1_zf : 8'bz;  // Controlled_Buffer controlled_buffer_10
  Register H (.D(controlled_buffer_1_out), .en(1'b0), .clk(CLK), .Q(H_q));  // open: clr
  Register L (.D(controlled_buffer_1_out), .en(1'b0), .clk(CLK), .Q(L_q));  // open: clr
  assign controlled_buffer_1_out = 1'b0 ? H_q : 8'bz;  // Controlled_Buffer controlled_buffer_11
  assign controlled_buffer_1_out = 1'b0 ? L_q : 8'bz;  // Controlled_Buffer controlled_buffer_12
  Register PCL (.D(controlled_buffer_13_out), .en(1'b0), .clk(CLK), .Q(PCL_q));  // open: clr
  assign controlled_buffer_13_out = 1'b0 ? PCL_q : 8'bz;  // Controlled_Buffer controlled_buffer_13
  assign controlled_buffer_13_out = 1'b0 ? H_q : 8'bz;  // Controlled_Buffer controlled_buffer_14
  assign controlled_buffer_15_out = 1'b0 ? L_q : 8'bz;  // Controlled_Buffer controlled_buffer_15
  Register PCH (.D(controlled_buffer_15_out), .en(1'b0), .clk(CLK), .Q(PCH_q));  // open: clr
  assign controlled_buffer_15_out = 1'b0 ? PCH_q : 8'bz;  // Controlled_Buffer controlled_buffer_16
  assign controlled_buffer_17_out = 1'b0 ? controlled_buffer_1_out : 8'bz;  // Controlled_Buffer controlled_buffer_17
  assign controlled_buffer_1_out = 1'b0 ? mem_1_d_out : 8'bz;  // Controlled_Buffer controlled_buffer_18
  mem mem_1 (
    .ADDR({controlled_buffer_15_out, controlled_buffer_13_out}), .WE(1'b0), .CLK(CLK),
    .D_in(controlled_buffer_17_out), .D_Out(mem_1_d_out));
endmodule

module dflop (
  input  D,
  input  clk,
  output Q1,
  output Q2
);

  wire and_1_out, and_2_out, not_1_out;

  not not_1 (not_1_out, D);
  and and_1 (and_1_out, not_1_out, clk);
  and and_2 (and_2_out, clk, D);
  nor nor_1 (Q1, and_1_out, Q2);
  nor nor_2 (Q2, Q1, and_2_out);

  // Notes on the sheet:
  //   clk: pull=up
endmodule

module reg1 (
  input  RE,
  input  D,
  input  clk,
  output Q
);

  wire and_1_out, and_2_out, not_1_out, or_1_out;

  not not_1 (not_1_out, RE);
  and and_1 (and_1_out, Q, not_1_out);
  and and_2 (and_2_out, RE, D);
  or or_1 (or_1_out, and_1_out, and_2_out);
  dflop dflop_1 (.D(or_1_out), .clk(clk), .Q1(Q));  // open: Q2
endmodule

module reg8 (
  input  RE,
  input  CLK,
  input  D0,
  input  D1,
  input  D2,
  input  D3,
  input  D4,
  input  D5,
  input  D6,
  input  D7,
  output Q0,
  output Q1,
  output Q2,
  output Q3,
  output Q4,
  output Q5,
  output Q6,
  output Q7
);

  reg1 reg1_1 (.RE(RE), .D(D0), .clk(CLK), .Q(Q0));
  reg1 reg1_2 (.RE(RE), .D(D1), .clk(CLK), .Q(Q1));
  reg1 reg1_3 (.RE(RE), .D(D2), .clk(CLK), .Q(Q2));
  reg1 reg1_4 (.RE(RE), .D(D3), .clk(CLK), .Q(Q3));
  reg1 reg1_5 (.RE(RE), .D(D4), .clk(CLK), .Q(Q4));
  reg1 reg1_6 (.RE(RE), .D(D5), .clk(CLK), .Q(Q5));
  reg1 reg1_7 (.RE(RE), .D(D6), .clk(CLK), .Q(Q6));
  reg1 reg1_8 (.RE(RE), .D(D7), .clk(CLK), .Q(Q7));
endmodule

module reg1ic (
  input  RE,
  input  D,
  input  CLK,
  output Q
);

  wire n7404_1_pin1, n7404_1_pin2, n7404_1_pin9, n7408_1_pin1, n7408_1_pin3, n7408_1_pin5, n7408_1_pin6,
       n7408_1_pin8, n7408_1_pin9, n7408_1_pin11;

  _7408 u_7408_1 (
    .pin1(n7408_1_pin1), .pin2(CLK), .pin3(n7408_1_pin3), .pin4(CLK), .pin5(n7408_1_pin5),
    .pin6(n7408_1_pin6), .pin13(D), .pin12(RE), .pin11(n7408_1_pin11), .pin10(Q), .pin9(n7408_1_pin9),
    .pin8(n7408_1_pin8));
  _7404 u_7404_1 (
    .pin1(n7404_1_pin1), .pin2(n7404_1_pin2), .pin13(RE), .pin12(n7408_1_pin9), .pin11(n7408_1_pin5),
    .pin10(n7408_1_pin1), .pin9(n7404_1_pin9), .pin8(Q));  // open: pin3, pin4, pin5, pin6
  _7432 u_7432_1 (
    .pin1(n7408_1_pin3), .pin2(n7404_1_pin2), .pin3(n7404_1_pin9), .pin4(n7408_1_pin6), .pin5(Q),
    .pin6(n7404_1_pin1), .pin13(n7408_1_pin11), .pin12(n7408_1_pin8), .pin11(n7408_1_pin5));  // open: pin10, pin9, pin8
endmodule

module reg8ic (
  input  RE,
  input  CLK,
  input  D0,
  input  D1,
  input  D2,
  input  D3,
  input  D4,
  input  D5,
  input  D6,
  input  D7,
  output Q0,
  output Q1,
  output Q2,
  output Q3,
  output Q4,
  output Q5,
  output Q6,
  output Q7
);

  reg1ic reg1ic_1 (.RE(RE), .D(D0), .CLK(CLK), .Q(Q0));
  reg1ic reg1ic_2 (.RE(RE), .D(D1), .CLK(CLK), .Q(Q1));
  reg1ic reg1ic_3 (.RE(RE), .D(D2), .CLK(CLK), .Q(Q2));
  reg1ic reg1ic_4 (.RE(RE), .D(D3), .CLK(CLK), .Q(Q3));
  reg1ic reg1ic_5 (.RE(RE), .D(D4), .CLK(CLK), .Q(Q4));
  reg1ic reg1ic_6 (.RE(RE), .D(D5), .CLK(CLK), .Q(Q5));
  reg1ic reg1ic_7 (.RE(RE), .D(D6), .CLK(CLK), .Q(Q6));
  reg1ic reg1ic_8 (.RE(RE), .D(D7), .CLK(CLK), .Q(Q7));
endmodule

module alu (
  input  CLK,
  input  CS,
  input  SUB,
  input  CF_in,
  input  BF_in,
  input  [7:0] A,
  input  [7:0] B,
  output CF,
  output BF,
  output ZF,
  output [7:0] Q
);

  wire and_1_out, and_2_out, and_3_out, and_4_out, and_5_out, and_6_out, and_7_out, and_8_out, and_9_out,
       and_10_out, and_11_out, and_12_out, and_13_out, and_14_out, and_15_out, and_16_out, multiplexer_1_out,
       nor_1_out, nor_2_out, nor_3_out, nor_4_out, nor_5_out, nor_6_out, not_1_out, not_2_out, not_3_out, Q0,
       Q1, Q2, Q3, Q4, Q5, Q6, Q7, xor_1_out, xor_2_out, xor_3_out, xor_4_out, xor_5_out, xor_6_out,
       xor_7_out, xor_8_out, xor_9_out, xor_11_out, xor_12_out, xor_14_out, xor_15_out, xor_17_out,
       xor_18_out, xor_20_out, xor_21_out, xor_23_out, xor_24_out, xor_26_out, xor_27_out, xor_29_out,
       xor_30_out, xor_32_out;

  Multiplexer multiplexer_1 (.in0(CF_in), .in1(not_1_out), .out(multiplexer_1_out), .sel(SUB));
  not not_1 (not_1_out, BF_in);
  xor xor_1 (xor_1_out, B[0], SUB);
  xor xor_2 (xor_2_out, SUB, B[1]);
  xor xor_3 (xor_3_out, B[2], SUB);
  xor xor_4 (xor_4_out, SUB, B[3]);
  xor xor_5 (xor_5_out, B[4], SUB);
  xor xor_6 (xor_6_out, SUB, B[5]);
  xor xor_7 (xor_7_out, B[6], SUB);
  xor xor_8 (xor_8_out, SUB, B[7]);
  xor xor_9 (xor_9_out, multiplexer_1_out, A[0]);
  and and_1 (and_1_out, multiplexer_1_out, A[0]);
  xor xor_10 (Q0, xor_9_out, xor_1_out);
  and and_2 (and_2_out, xor_1_out, xor_9_out);
  xor xor_11 (xor_11_out, and_1_out, and_2_out);
  xor xor_12 (xor_12_out, xor_11_out, A[1]);
  and and_3 (and_3_out, xor_11_out, A[1]);
  xor xor_13 (Q1, xor_12_out, xor_2_out);
  and and_4 (and_4_out, xor_2_out, xor_12_out);
  nor nor_1 (nor_1_out, Q0, Q1);
  xor xor_14 (xor_14_out, and_3_out, and_4_out);
  xor xor_15 (xor_15_out, xor_14_out, A[2]);
  and and_5 (and_5_out, xor_14_out, A[2]);
  xor xor_16 (Q2, xor_15_out, xor_3_out);
  and and_6 (and_6_out, xor_3_out, xor_15_out);
  nor nor_2 (nor_2_out, nor_1_out, Q2);
  xor xor_17 (xor_17_out, and_5_out, and_6_out);
  xor xor_18 (xor_18_out, xor_17_out, A[3]);
  and and_7 (and_7_out, xor_17_out, A[3]);
  xor xor_19 (Q3, xor_18_out, xor_4_out);
  and and_8 (and_8_out, xor_4_out, xor_18_out);
  nor nor_3 (nor_3_out, nor_2_out, Q3);
  xor xor_20 (xor_20_out, and_7_out, and_8_out);
  xor xor_21 (xor_21_out, xor_20_out, A[4]);
  and and_9 (and_9_out, xor_20_out, A[4]);
  xor xor_22 (Q4, xor_21_out, xor_5_out);
  and and_10 (and_10_out, xor_5_out, xor_21_out);
  nor nor_4 (nor_4_out, nor_3_out, Q4);
  xor xor_23 (xor_23_out, and_9_out, and_10_out);
  xor xor_24 (xor_24_out, xor_23_out, A[5]);
  and and_11 (and_11_out, xor_23_out, A[5]);
  xor xor_25 (Q5, xor_24_out, xor_6_out);
  and and_12 (and_12_out, xor_6_out, xor_24_out);
  nor nor_5 (nor_5_out, nor_4_out, Q5);
  xor xor_26 (xor_26_out, and_11_out, and_12_out);
  xor xor_27 (xor_27_out, xor_26_out, A[6]);
  and and_13 (and_13_out, xor_26_out, A[6]);
  xor xor_28 (Q6, xor_27_out, xor_7_out);
  and and_14 (and_14_out, xor_7_out, xor_27_out);
  nor nor_6 (nor_6_out, nor_5_out, Q6);
  xor xor_29 (xor_29_out, and_13_out, and_14_out);
  xor xor_30 (xor_30_out, xor_29_out, A[7]);
  and and_15 (and_15_out, xor_29_out, A[7]);
  xor xor_31 (Q7, xor_30_out, xor_8_out);
  and and_16 (and_16_out, xor_8_out, xor_30_out);
  nor nor_7 (ZF, nor_6_out, Q7);
  xor xor_32 (xor_32_out, and_15_out, and_16_out);
  not not_2 (not_2_out, SUB);
  and and_17 (CF, not_2_out, xor_32_out);
  not not_3 (not_3_out, xor_32_out);
  and and_18 (BF, SUB, not_3_out);
  Register ALU_RES (.D({Q7, Q6, Q5, Q4, Q3, Q2, Q1, Q0}), .en(CS), .clk(CLK), .Q(Q));  // open: clr
endmodule

module bitadd (
  input  C_in,
  input  A,
  input  B,
  output Q,
  output C_out
);

  wire and_1_out, and_2_out, xor_1_out;

  xor xor_1 (xor_1_out, A, C_in);
  and and_1 (and_1_out, C_in, A);
  xor xor_2 (Q, xor_1_out, B);
  and and_2 (and_2_out, B, xor_1_out);
  xor xor_3 (C_out, and_1_out, and_2_out);
endmodule

module mem (
  input  [15:0] ADDR,
  input  WE,
  input  CLK,
  input  [7:0] D_in,
  output [7:0] D_Out
);

  wire [7:0] ram_1_dout, rom_1_data;

  RAM #(.addrWidth(16), .enables("line")) ram_1 (.addr(ADDR), .we(WE), .clk(CLK), .din(D_in), .dout(ram_1_dout));
  ROM #(.addrWidth(15)) rom_1 (.addr(ADDR[14:0]), .data(rom_1_data));
  Multiplexer #(.width(8)) multiplexer_1 (.in0(rom_1_data), .in1(ram_1_dout), .out(D_Out), .sel(ADDR[15]));
endmodule
